# Fritzing sketch sagsolmesafe (saved by Fritzing 0.9.2b)
breadboards: 1

parts:
  Eleman1 = Arduino Uno (Rev3)
  M1 = DC Motor
  M2 = DC Motor  # not connected
  M3 = DC Motor  # not connected
  M4 = DC Motor
  S1 = H-Bridge with L298N
  BAT1 = BC9VPC [package=bc9vpc]
  Eleman2 = SRF05 Ultrasonic Rangefinder
  Eleman3 = SRF05 Ultrasonic Rangefinder
  Eleman4 = SRF05 Ultrasonic Rangefinder

nets:
  N1: Eleman1.D8, S1.IN2
  N2: Eleman1.D9_PWM, S1.IN1
  N3: Eleman1.D10_PWM/SS, S1.ENB
  N4: Eleman1.D11_PWM/MOSI, S1.ENA
  N5: Eleman1.D12/MISO, S1.IN4
  N6: Eleman1.D13/SCK, S1.IN3
  N7: Eleman1.D2, Eleman2.Echo
  N8: Eleman1.D3_PWM, Eleman2.Trig
  N9: Eleman1.D4, Eleman3.Echo
  N10: Eleman1.D5_PWM, Eleman3.Trig
  N11: Eleman1.D6_PWM, Eleman4.Echo
  N12: Eleman1.D7, Eleman4.Trig
  GND: Eleman1.GND, S1.GND, BAT1.V-
  VIN: Eleman1.VIN, S1.12V, BAT1.V+
  N13: M1.pin_1, S1.M1-02
  N14: M1.pin_2, S1.M1-01
  N15: M4.pin_1, S1.M2-01
  N16: M4.pin_2, S1.M2-02
  VCC: Eleman3.VCC, Eleman4.VCC
  GND_2: Eleman3.GND, Eleman4.GND

notes:
  1 nolu sol sensör
  3 nolu sağ sensör
  2 nolu ön sensör
  Giriş voltajı olarak üç tane 3.7V'luk lityum iyon pil kullandım. Dikkat edilmesi gereken, bread boardın üst tarafı 11.1V, alt tarafı da 5V'dur. Arduinonun beslemesini Vin girişinden yaptım. Arduinonun 5V çıkışını sensörleri beslemek için kullandım. Sensörleri 5V tan fazla vermeyin, yanar.
  Araç öne gitmesi gerekirken arkaya, yada düz gitmei gerekirsen sağa yada sola giderse motorları ters bağlanmıştır. Ya motorların ucunu değiştirin yada sagileri, saggeri ile solileri, solgeri pinlerinin numaralarını yer değiştirin. Hangisi kolayınıza gelirse.
  Sensör açılarını kendinize uygun bir şekilde ayarlayın, ben aşağı yukarı 55 derece yaptım.

custom parts:
  H-Bridge with L298N: h-bridge
